// Logisim project 1_z_ohyr.circ as structural Verilog: 1 circuit, main circuit main
module main (
  input  A,
  input  B,
  input  C,
  input  D,
  output Y_zad,
  output Z_zad,
  output Y_DNF,
  output Z_DNF,
  output Y_KNF,
  output Z_KNF
);

  wire and_1_out, B_C_out, C__nD_out, nB___nC__D_out, nC__D_out, nor_1_out, not_1_out, not_2_out, not_3_out,
       not_4_out, not_5_out, xor_1_out;

  not not_1 (not_1_out, C);
  not not_2 (not_2_out, D);
  not not_3 (not_3_out, B);
  not not_4 (not_4_out, C);
  not not_5 (not_5_out, D);
  and nC__D (nC__D_out, not_1_out, D);
  and C__nD (C__nD_out, C, not_2_out);
  nor nor_1 (nor_1_out, A, B);
  xor xor_1 (xor_1_out, C, not_5_out);
  and and_1 (and_1_out, B, D);
  and B_C (B_C_out, B, C);
  and nB___nC__D (nB___nC__D_out, not_3_out, not_4_out, D);
  nand nand_1 (Y_zad, nor_1_out, xor_1_out);
  xnor xnor_1 (Z_zad, xor_1_out, and_1_out);
  or or_1 (Y_DNF, A, B, C__nD_out, nC__D_out);
  or or_2 (Z_DNF, B_C_out, C__nD_out, nB___nC__D_out);
endmodule
